// Logisim project 10-12.circ as structural Verilog: 1 circuit, main circuit main
module main (
  input  in_1,
  input  in_2,
  output out_3
);

  wire and_1_out, not_1_out, or_1_out;

  not not_1 (not_1_out, and_1_out);
  and and_1 (and_1_out, in_1, in_2);
  or or_1 (or_1_out, in_1, in_2);
  and and_2 (out_3, not_1_out, or_1_out);
endmodule
